// Logisim project tennis.circ as structural Verilog: 18 circuits, main circuit main
module main (
);

  wire leds_1_out_3, leds_1_out_4, leds_1_out_5, leds_1_out_6, leds_1_out_7, leds_1_out_8, leds_1_out_9,
       leds_1_out_10, leds_1_out_11, leds_1_out_12, leds_1_out_13, leds_1_out_14, leds_1_out_15,
       leds_1_out_16, leds_1_out_17, leds_1_out_18, leds_1_out_19, leds_1_out_20, leds_1_out_21,
       leds_1_out_22, leds_1_out_23, leds_1_out_24, leds_1_out_25, leds_1_out_26, leds_1_out_27,
       leds_1_out_28, leds_1_out_29, leds_1_out_30, leds_1_out_31, leds_1_out_32, leds_1_out_33,
       leds_1_out_34, Reset_out;
  wire [1:0] joystick_1_y;
  wire [3:0] clock_1_tens, clock_1_units, clock_2_tens, clock_2_units;
  wire [4:0] kinematic_controller_1_ballx, kinematic_controller_1_bally, kinematic_controller_1_leftyout,
       kinematic_controller_1_out_3, kinematic_controller_1_rightyout, video_section_1_out_14,
       video_section_1_out_15, video_section_1_out_16, video_section_1_out_17, video_section_1_out_18,
       video_section_2_out_14, video_section_2_out_15, video_section_2_out_16, video_section_2_out_17,
       video_section_2_out_18, video_section_3_out_14, video_section_3_out_15, video_section_3_out_16,
       video_section_3_out_17, video_section_3_out_18;
  wire [7:0] cdm8_score, player_score;
  wire [31:0] video_section_1_out_6, video_section_1_out_7, video_section_1_out_8, video_section_1_out_9,
       video_section_1_out_10, video_section_1_out_11, video_section_1_out_12, video_section_1_out_13,
       video_section_2_out_6, video_section_2_out_7, video_section_2_out_8, video_section_2_out_9,
       video_section_2_out_10, video_section_2_out_11, video_section_2_out_12, video_section_2_out_13,
       video_section_3_out_6, video_section_3_out_7, video_section_3_out_8, video_section_3_out_9,
       video_section_3_out_10, video_section_3_out_11, video_section_3_out_12, video_section_3_out_13,
       video_section_4_out_6, video_section_4_out_7, video_section_4_out_8, video_section_4_out_9,
       video_section_4_out_10, video_section_4_out_11, video_section_4_out_12, video_section_4_out_13;

  leds leds_1 (
    .in_1(player_score), .in_2(cdm8_score), .out_33(leds_1_out_33), .out_31(leds_1_out_31),
    .out_29(leds_1_out_29), .out_27(leds_1_out_27), .out_25(leds_1_out_25), .out_23(leds_1_out_23),
    .out_21(leds_1_out_21), .out_19(leds_1_out_19), .out_3(leds_1_out_3), .out_5(leds_1_out_5),
    .out_7(leds_1_out_7), .out_9(leds_1_out_9), .out_11(leds_1_out_11), .out_13(leds_1_out_13),
    .out_15(leds_1_out_15), .out_17(leds_1_out_17), .out_4(leds_1_out_4), .out_6(leds_1_out_6),
    .out_8(leds_1_out_8), .out_10(leds_1_out_10), .out_12(leds_1_out_12), .out_14(leds_1_out_14),
    .out_16(leds_1_out_16), .out_18(leds_1_out_18), .out_20(leds_1_out_20), .out_22(leds_1_out_22),
    .out_24(leds_1_out_24), .out_26(leds_1_out_26), .out_28(leds_1_out_28), .out_30(leds_1_out_30),
    .out_32(leds_1_out_32), .out_34(leds_1_out_34));
  LED led_1 (.in(leds_1_out_33));
  LED led_2 (.in(leds_1_out_4));
  LED led_3 (.in(leds_1_out_29));
  LED led_4 (.in(leds_1_out_31));
  LED led_5 (.in(leds_1_out_6));
  LED led_6 (.in(leds_1_out_8));
  clock clock_1 (.\input (player_score), .tens(clock_1_tens), .units(clock_1_units));
  Hex_Digit_Display hex_digit_display_1 (.value(clock_1_tens));  // open: dp
  Joystick #(.bits(2)) joystick_1 (.y(joystick_1_y));  // open: x
  LED led_7 (.in(leds_1_out_25));
  LED led_8 (.in(leds_1_out_27));
  LED led_9 (.in(leds_1_out_12));
  LED led_10 (.in(leds_1_out_10));
  Hex_Digit_Display hex_digit_display_2 (.value(clock_1_units));  // open: dp
  Button Reset (.out(Reset_out));
  DotMatrix #(.matrixcols(32), .matrixrows(32)) dotmatrix_1 (
    .col0(video_section_1_out_6), .col1(video_section_1_out_7), .col2(video_section_1_out_8),
    .col3(video_section_1_out_9), .col4(video_section_1_out_10), .col5(video_section_1_out_11),
    .col6(video_section_1_out_12), .col7(video_section_1_out_13), .col8(video_section_2_out_6),
    .col9(video_section_2_out_7), .col10(video_section_2_out_8), .col11(video_section_2_out_9),
    .col12(video_section_2_out_10), .col13(video_section_2_out_11), .col14(video_section_2_out_12),
    .col15(video_section_2_out_13), .col16(video_section_3_out_6), .col17(video_section_3_out_7),
    .col18(video_section_3_out_8), .col19(video_section_3_out_9), .col20(video_section_3_out_10),
    .col21(video_section_3_out_11), .col22(video_section_3_out_12), .col23(video_section_3_out_13),
    .col24(video_section_4_out_6), .col25(video_section_4_out_7), .col26(video_section_4_out_8),
    .col27(video_section_4_out_9), .col28(video_section_4_out_10), .col29(video_section_4_out_11),
    .col30(video_section_4_out_12), .col31(video_section_4_out_13));
  kinematic_controller kinematic_controller_1 (
    .button_up(joystick_1_y), .out_3(kinematic_controller_1_out_3), .ballX(kinematic_controller_1_ballx),
    .ballY(kinematic_controller_1_bally), .leftYout(kinematic_controller_1_leftyout),
    .rightYout(kinematic_controller_1_rightyout), .reset(Reset_out), .out_8(player_score), .out_9(cdm8_score));
  LED led_11 (.in(leds_1_out_23));
  LED led_12 (.in(leds_1_out_21));
  LED led_13 (.in(leds_1_out_16));
  LED led_14 (.in(leds_1_out_14));
  video_section video_section_1 (
    .in_1(kinematic_controller_1_out_3), .in_2(kinematic_controller_1_ballx),
    .in_3(kinematic_controller_1_bally), .in_4(kinematic_controller_1_leftyout),
    .in_5(kinematic_controller_1_rightyout), .out_14(video_section_1_out_14),
    .out_15(video_section_1_out_15), .out_16(video_section_1_out_16), .out_17(video_section_1_out_17),
    .out_18(video_section_1_out_18), .out_6(video_section_1_out_6), .out_7(video_section_1_out_7),
    .out_8(video_section_1_out_8), .out_9(video_section_1_out_9), .out_10(video_section_1_out_10),
    .out_11(video_section_1_out_11), .out_12(video_section_1_out_12), .out_13(video_section_1_out_13));
  LED led_15 (.in(leds_1_out_17));
  LED led_16 (.in(leds_1_out_19));
  LED led_17 (.in(leds_1_out_18));
  LED led_18 (.in(leds_1_out_20));
  video_section video_section_2 (
    .in_1(video_section_1_out_14), .in_2(video_section_1_out_15), .in_3(video_section_1_out_16),
    .in_4(video_section_1_out_17), .in_5(video_section_1_out_18), .out_14(video_section_2_out_14),
    .out_15(video_section_2_out_15), .out_16(video_section_2_out_16), .out_17(video_section_2_out_17),
    .out_18(video_section_2_out_18), .out_6(video_section_2_out_6), .out_7(video_section_2_out_7),
    .out_8(video_section_2_out_8), .out_9(video_section_2_out_9), .out_10(video_section_2_out_10),
    .out_11(video_section_2_out_11), .out_12(video_section_2_out_12), .out_13(video_section_2_out_13));
  LED led_19 (.in(leds_1_out_15));
  LED led_20 (.in(leds_1_out_13));
  LED led_21 (.in(leds_1_out_22));
  LED led_22 (.in(leds_1_out_24));
  video_section video_section_3 (
    .in_1(video_section_2_out_14), .in_2(video_section_2_out_15), .in_3(video_section_2_out_16),
    .in_4(video_section_2_out_17), .in_5(video_section_2_out_18), .out_14(video_section_3_out_14),
    .out_15(video_section_3_out_15), .out_16(video_section_3_out_16), .out_17(video_section_3_out_17),
    .out_18(video_section_3_out_18), .out_6(video_section_3_out_6), .out_7(video_section_3_out_7),
    .out_8(video_section_3_out_8), .out_9(video_section_3_out_9), .out_10(video_section_3_out_10),
    .out_11(video_section_3_out_11), .out_12(video_section_3_out_12), .out_13(video_section_3_out_13));
  LED led_23 (.in(leds_1_out_9));
  LED led_24 (.in(leds_1_out_11));
  LED led_25 (.in(leds_1_out_26));
  LED led_26 (.in(leds_1_out_28));
  Hex_Digit_Display hex_digit_display_3 (.value(clock_2_tens));  // open: dp
  clock clock_2 (.\input (cdm8_score), .tens(clock_2_tens), .units(clock_2_units));
  video_section video_section_4 (
    .in_1(video_section_3_out_14), .in_2(video_section_3_out_15), .in_3(video_section_3_out_16),
    .in_4(video_section_3_out_17), .in_5(video_section_3_out_18), .out_6(video_section_4_out_6),
    .out_7(video_section_4_out_7), .out_8(video_section_4_out_8), .out_9(video_section_4_out_9),
    .out_10(video_section_4_out_10), .out_11(video_section_4_out_11), .out_12(video_section_4_out_12),
    .out_13(video_section_4_out_13));  // open: out_14, out_15, out_16, out_17, out_18
  LED led_27 (.in(leds_1_out_5));
  LED led_28 (.in(leds_1_out_7));
  LED led_29 (.in(leds_1_out_32));
  LED led_30 (.in(leds_1_out_30));
  Hex_Digit_Display hex_digit_display_4 (.value(clock_2_units));  // open: dp
  LED led_31 (.in(leds_1_out_3));
  LED led_32 (.in(leds_1_out_34));
endmodule

module video_chip (
  input  [4:0] chipID,
  input  [4:0] ballX,
  input  [4:0] ballY,
  input  [4:0] leftBat,
  input  [4:0] rightBat,
  output [4:0] nextChipID,
  output [4:0] ballX_2,
  output [4:0] ballY_2,
  output [4:0] leftBat_2,
  output [4:0] rightBat_2
);

  inc_5_bit inc_5_bit_1 (.in_1(chipID), .out_2(nextChipID));

  assign ballX_2 = ballX;
  assign ballY_2 = ballY;
  assign leftBat_2 = leftBat;
  assign rightBat_2 = rightBat;
endmodule

// inc
module inc_5_bit (
  input  [4:0] in_1,
  output [4:0] out_2
);

  wire [4:0] and_1_out;

  assign and_1_out = {and_1_out[3:0], 1'b1} & in_1;  // AND_Gate and_1, 5 bits wide
  assign out_2 = in_1 ^ {and_1_out[3:0], 1'b1};  // XOR_Gate xor_1, 5 bits wide
  // also tied to GND on the sheet: and_1_out[4]
endmodule

module video_section (
  input  [4:0] in_1,
  input  [4:0] in_2,
  input  [4:0] in_3,
  input  [4:0] in_4,
  input  [4:0] in_5,
  output [31:0] out_6,
  output [31:0] out_7,
  output [31:0] out_8,
  output [31:0] out_9,
  output [31:0] out_10,
  output [31:0] out_11,
  output [31:0] out_12,
  output [31:0] out_13,
  output [4:0] out_14,
  output [4:0] out_15,
  output [4:0] out_16,
  output [4:0] out_17,
  output [4:0] out_18
);

  wire comparator_1_eq, comparator_2_eq, comparator_3_eq, comparator_4_eq, comparator_5_eq, comparator_6_eq,
       comparator_7_eq, comparator_8_eq, comparator_9_eq, comparator_10_eq, not_1_out, not_2_out;
  wire [4:0] ID1, ID2, ID3, ID4, ID5, ID6, ID7, video_chip_1_ballx_2, video_chip_1_bally_2,
       video_chip_1_leftbat_2, video_chip_1_rightbat_2, video_chip_2_ballx_2, video_chip_2_bally_2,
       video_chip_2_leftbat_2, video_chip_2_rightbat_2, video_chip_3_ballx_2, video_chip_3_bally_2,
       video_chip_3_leftbat_2, video_chip_3_rightbat_2, video_chip_4_ballx_2, video_chip_4_bally_2,
       video_chip_4_leftbat_2, video_chip_4_rightbat_2, video_chip_5_ballx_2, video_chip_5_bally_2,
       video_chip_5_leftbat_2, video_chip_5_rightbat_2, video_chip_6_ballx_2, video_chip_6_bally_2,
       video_chip_6_leftbat_2, video_chip_6_rightbat_2, video_chip_7_ballx_2, video_chip_7_bally_2,
       video_chip_7_leftbat_2, video_chip_7_rightbat_2;
  wire [31:0] bat_l_32, bat_r_32, multiplexer_2_out, multiplexer_3_out, multiplexer_8_out, multiplexer_9_out,
       y;

  Multiplexer #(.width(32)) multiplexer_1 (.in0({32{1'b0}}), .in1(y), .out(out_6), .sel(comparator_1_eq));  // open: en
  _5_to_32 u_5_to_32_1 (.in_1(in_3), .out_2(y));
  Multiplexer #(.width(32)) multiplexer_2 (
    .in0(bat_l_32), .in1({32{1'b0}}), .out(multiplexer_2_out), .sel(not_1_out));  // open: en
  Comparator #(.width(5)) comparator_1 (.a(in_1), .b(in_2), .eq(comparator_1_eq));  // open: gt, lt
  video_chip video_chip_1 (
    .chipID(in_1), .ballX(in_2), .ballY(in_3), .leftBat(in_4), .rightBat(in_5), .nextChipID(ID1),
    .ballX_2(video_chip_1_ballx_2), .ballY_2(video_chip_1_bally_2), .leftBat_2(video_chip_1_leftbat_2),
    .rightBat_2(video_chip_1_rightbat_2));
  assign out_7 = multiplexer_2_out | multiplexer_3_out;  // OR_Gate or_1, 32 bits wide
  not not_1 (not_1_out, comparator_3_eq);
  Multiplexer #(.width(32)) multiplexer_3 (
    .in0({32{1'b0}}), .in1(y), .out(multiplexer_3_out), .sel(comparator_2_eq));  // open: en
  Comparator #(.width(5)) comparator_2 (.a(ID1), .b(in_2), .eq(comparator_2_eq));  // open: gt, lt
  Comparator #(.width(5)) comparator_3 (.a(ID1), .b(5'b00001), .eq(comparator_3_eq));  // open: gt, lt
  bat bat_1 (.in_1(out_17), .out_2(bat_l_32));
  Multiplexer #(.width(32)) multiplexer_4 (.in0({32{1'b0}}), .in1(y), .out(out_8), .sel(comparator_4_eq));  // open: en
  Comparator #(.width(5)) comparator_4 (.a(ID2), .b(in_2), .eq(comparator_4_eq));  // open: gt, lt
  video_chip video_chip_2 (
    .chipID(ID1), .ballX(video_chip_1_ballx_2), .ballY(video_chip_1_bally_2),
    .leftBat(video_chip_1_leftbat_2), .rightBat(video_chip_1_rightbat_2), .nextChipID(ID2),
    .ballX_2(video_chip_2_ballx_2), .ballY_2(video_chip_2_bally_2), .leftBat_2(video_chip_2_leftbat_2),
    .rightBat_2(video_chip_2_rightbat_2));
  Multiplexer #(.width(32)) multiplexer_5 (.in0({32{1'b0}}), .in1(y), .out(out_9), .sel(comparator_5_eq));  // open: en
  Comparator #(.width(5)) comparator_5 (.a(ID3), .b(in_2), .eq(comparator_5_eq));  // open: gt, lt
  video_chip video_chip_3 (
    .chipID(ID2), .ballX(video_chip_2_ballx_2), .ballY(video_chip_2_bally_2),
    .leftBat(video_chip_2_leftbat_2), .rightBat(video_chip_2_rightbat_2), .nextChipID(ID3),
    .ballX_2(video_chip_3_ballx_2), .ballY_2(video_chip_3_bally_2), .leftBat_2(video_chip_3_leftbat_2),
    .rightBat_2(video_chip_3_rightbat_2));
  Multiplexer #(.width(32)) multiplexer_6 (.in0({32{1'b0}}), .in1(y), .out(out_10), .sel(comparator_6_eq));  // open: en
  video_chip video_chip_4 (
    .chipID(ID3), .ballX(video_chip_3_ballx_2), .ballY(video_chip_3_bally_2),
    .leftBat(video_chip_3_leftbat_2), .rightBat(video_chip_3_rightbat_2), .nextChipID(ID4),
    .ballX_2(video_chip_4_ballx_2), .ballY_2(video_chip_4_bally_2), .leftBat_2(video_chip_4_leftbat_2),
    .rightBat_2(video_chip_4_rightbat_2));
  Comparator #(.width(5)) comparator_6 (.a(ID4), .b(in_2), .eq(comparator_6_eq));  // open: gt, lt
  video_chip video_chip_5 (
    .chipID(ID4), .ballX(video_chip_4_ballx_2), .ballY(video_chip_4_bally_2),
    .leftBat(video_chip_4_leftbat_2), .rightBat(video_chip_4_rightbat_2), .nextChipID(ID5),
    .ballX_2(video_chip_5_ballx_2), .ballY_2(video_chip_5_bally_2), .leftBat_2(video_chip_5_leftbat_2),
    .rightBat_2(video_chip_5_rightbat_2));
  Multiplexer #(.width(32)) multiplexer_7 (.in0({32{1'b0}}), .in1(y), .out(out_11), .sel(comparator_7_eq));  // open: en
  Comparator #(.width(5)) comparator_7 (.a(ID5), .b(in_2), .eq(comparator_7_eq));  // open: gt, lt
  video_chip video_chip_6 (
    .chipID(ID5), .ballX(video_chip_5_ballx_2), .ballY(video_chip_5_bally_2),
    .leftBat(video_chip_5_leftbat_2), .rightBat(video_chip_5_rightbat_2), .nextChipID(ID6),
    .ballX_2(video_chip_6_ballx_2), .ballY_2(video_chip_6_bally_2), .leftBat_2(video_chip_6_leftbat_2),
    .rightBat_2(video_chip_6_rightbat_2));
  assign out_12 = multiplexer_8_out | multiplexer_9_out;  // OR_Gate or_2, 32 bits wide
  Multiplexer #(.width(32)) multiplexer_8 (
    .in0(bat_r_32), .in1({32{1'b0}}), .out(multiplexer_8_out), .sel(not_2_out));  // open: en
  Multiplexer #(.width(32)) multiplexer_9 (
    .in0({32{1'b0}}), .in1(y), .out(multiplexer_9_out), .sel(comparator_8_eq));  // open: en
  Comparator #(.width(5)) comparator_8 (.a(ID6), .b(in_2), .eq(comparator_8_eq));  // open: gt, lt
  Comparator #(.width(5), .mode("unsigned")) comparator_9 (
    .a(ID6), .b(5'b11110), .eq(comparator_9_eq));  // open: gt, lt
  bat bat_2 (.in_1(out_18), .out_2(bat_r_32));
  video_chip video_chip_7 (
    .chipID(ID6), .ballX(video_chip_6_ballx_2), .ballY(video_chip_6_bally_2),
    .leftBat(video_chip_6_leftbat_2), .rightBat(video_chip_6_rightbat_2), .nextChipID(ID7),
    .ballX_2(video_chip_7_ballx_2), .ballY_2(video_chip_7_bally_2), .leftBat_2(video_chip_7_leftbat_2),
    .rightBat_2(video_chip_7_rightbat_2));
  not not_2 (not_2_out, comparator_9_eq);
  Multiplexer #(.width(32)) multiplexer_10 (
    .in0({32{1'b0}}), .in1(y), .out(out_13), .sel(comparator_10_eq));  // open: en
  Comparator #(.width(5)) comparator_10 (.a(ID7), .b(in_2), .eq(comparator_10_eq));  // open: gt, lt
  video_chip video_chip_8 (
    .chipID(ID7), .ballX(video_chip_7_ballx_2), .ballY(video_chip_7_bally_2),
    .leftBat(video_chip_7_leftbat_2), .rightBat(video_chip_7_rightbat_2), .nextChipID(out_14),
    .ballX_2(out_15), .ballY_2(out_16), .leftBat_2(out_17), .rightBat_2(out_18));

  // Other names for the same wires on the sheet: bat_l[4:0] = out_17; bat_r[4:0] = out_18; ID0[4:0] = in_1;
  //   x[4:0] = in_2
endmodule

module inrange (
  input  [4:0] Yball,
  input  [4:0] Ybat,
  input  isTheSameX,
  output exit
);

  wire comparator_1_lt, comparator_2_gt, nor_1_out;
  wire [4:0] adder_1_out;

  // Probe on Yball
  // Probe on Ybat
  // Probe on adder_1_out
  Adder #(.width(5)) adder_1 (.a(5'b00011), .b(Ybat), .out(adder_1_out));  // open: cin, cout
  Comparator #(.width(5)) comparator_1 (.a(Yball), .b(Ybat), .lt(comparator_1_lt));  // open: gt, eq
  Comparator #(.width(5)) comparator_2 (.a(Yball), .b(adder_1_out), .gt(comparator_2_gt));  // open: eq, lt
  nor nor_1 (nor_1_out, comparator_1_lt, comparator_2_gt);
  assign exit = isTheSameX ? nor_1_out : 1'bz;  // Controlled_Buffer controlled_buffer_1
  Pull_Resistor pull_resistor_1 (.node(exit));
endmodule

// CONTROLLER
module kinematic_controller (
  input  reset,
  input  [1:0] button_up,
  output [4:0] out_3,
  output [4:0] ballX,
  output [4:0] ballY,
  output [4:0] leftYout,
  output [4:0] rightYout,
  output [7:0] out_8,
  output [7:0] out_9
);

  wire clock_1_out, clock_2_out, clock_3_out, clock_4_out, controlled_buffer_1_out, counter_3_q, down,
       hitTheLeftBall, hitTheRightBall, init, or_1_out, up, x, y;
  wire [2:0] left_bat_out, right_bat_out, x_ball, y_ball;
  wire [7:0] cdm8_1_out_9, cdm8_bat, left_bat_temp, multiplexer_1_out, multiplexer_2_out, multiplexer_3_out,
       multiplexer_4_out, right_bat, vx, vx_temp, vy, vy_temp, xball, yball;

  Comparator #(.width(2), .mode("unsigned")) comparator_1 (.a(2'b10), .b(button_up), .gt(up), .lt(down));  // open: eq
  bat_move bat_move_1 (.in_1({leftYout, left_bat_out}), .bat_y(left_bat_temp), .in_2(up), .in_3(down));
  check_hit check_hit_1 (
    .ball_x(xball), .x_hit(x), .left_bat(left_bat_temp), .vx(vx_temp), .vy(vy_temp), .ball_y(yball),
    .y_hit(y), .hitTheRightWall(hitTheRightBall), .hitTheLeftWall(hitTheLeftBall), .right_bat(right_bat));
  cdm8 cdm8_1 (
    .p_score(out_8), .cdm8_score(out_9), .ball_x(xball), .ball_y(yball), .vx(vx_temp), .vy(vy_temp),
    .out_8(cdm8_bat), .out_9(cdm8_1_out_9), .reset(reset));
  cdm8_bat_move cdm8_bat_move_1 (.out_3(right_bat), .current_y({rightYout, right_bat_out}), .new_y(cdm8_bat));
  Clock #(.highDuration(4), .lowDuration(4)) clock_1 (.out(clock_1_out));
  // Probe on cdm8_1_out_9
  Multiplexer #(.width(8)) multiplexer_1 (
    .in0({ballX, x_ball}), .in1(8'h78), .out(multiplexer_1_out), .sel(init));  // open: en
  Register xreg (.D(multiplexer_1_out), .Q(xball), .clk(clock_2_out));  // open: en, clr
  Register u_vx (.D(multiplexer_2_out), .Q(vx_temp), .clk(clock_2_out));  // open: en, clr
  Multiplexer #(.width(8)) multiplexer_2 (.in0(vx), .in1({8{1'b1}}), .out(multiplexer_2_out), .sel(init));  // open: en
  Clock #(.highDuration(2), .lowDuration(2)) clock_2 (.out(clock_2_out));
  Counter counter_1 (.count(hitTheRightBall), .Q(out_8), .clk(clock_2_out), .clr(reset));  // open: load, D, carry
  Register leftYreg (
    .D(left_bat_temp), .Q({leftYout, left_bat_out}), .clk(controlled_buffer_1_out), .clr(reset));  // open: en
  assign controlled_buffer_1_out = or_1_out ? clock_1_out : 1'bz;  // Controlled_Buffer controlled_buffer_1
  or or_1 (or_1_out, up, down);
  Multiplexer #(.width(8)) multiplexer_3 (
    .in0({ballY, y_ball}), .in1(8'h78), .out(multiplexer_3_out), .sel(init));  // open: en
  Multiplexer #(.width(8)) multiplexer_4 (.in0(vy), .in1(8'h2), .out(multiplexer_4_out), .sel(init));  // open: en
  Clock clock_3 (.out(clock_3_out));
  Register yreg (.D(multiplexer_3_out), .Q(yball), .clk(clock_2_out));  // open: en, clr
  Register u_vy (.D(multiplexer_4_out), .Q(vy_temp), .clk(clock_2_out));  // open: en, clr
  Counter counter_2 (.count(hitTheLeftBall), .Q(out_9), .clk(clock_2_out), .clr(reset));  // open: load, D, carry
  Register rightYreg (.D(right_bat), .Q({rightYout, right_bat_out}), .clk(clock_3_out), .clr(reset));  // open: en
  ball_move ball_move_1 (
    .crash_x(x), .crash_y(y), .vx(vx_temp), .vy(vy_temp), .ball_x(xball), .ball_y(yball),
    .ball_x_2({ballX, x_ball}), .ball_y_2({ballY, y_ball}), .new_vx(vx), .new_vy(vy));
  Clock #(.highDuration(4), .lowDuration(4)) clock_4 (.out(clock_4_out));
  Counter #(.width(1), .max('h1)) counter_3 (
    .count(init), .Q(counter_3_q), .clk(clock_4_out), .clr(reset));  // open: load, D, carry
  Comparator #(.width(1), .mode("unsigned")) comparator_2 (.a(1'b0), .b(counter_3_q), .eq(init));  // open: gt, lt

  assign out_3 = {5{1'b0}};

  // Other names for the same wires on the sheet: y_ball[7:3] = ballY; cdm8_score[7:0] = out_9;
  //   left_bat_out[7:3] = leftYout; player_score[7:0] = out_8; right_bat_out[7:3] = rightYout; x_ball[7:3] = ballX
endmodule

module inc_3_bit (
  input  [2:0] in_1,
  output [2:0] out_2
);

  wire [2:0] and_1_out;

  assign and_1_out = {and_1_out[1:0], 1'b1} & in_1;  // AND_Gate and_1, 3 bits wide
  assign out_2 = in_1 ^ {and_1_out[1:0], 1'b1};  // XOR_Gate xor_1, 3 bits wide
  // also tied to GND on the sheet: and_1_out[2]
endmodule

// conv
module _5_to_32 (
  input  [4:0] in_1,
  output [31:0] out_2
);

  Shifter #(.width(32)) shifter_1 (.in(32'h1), .\dist (in_1), .out(out_2));
endmodule

module bat (
  input  [4:0] in_1,
  output [31:0] out_2
);

  wire [31:0] adder_1_out, adder_2_out, n5_to_32_1_out_2, shifter_1_out, shifter_2_out, shifter_3_out;

  _5_to_32 u_5_to_32_1 (.in_1(in_1), .out_2(n5_to_32_1_out_2));
  Shifter #(.width(32)) shifter_1 (.in(n5_to_32_1_out_2), .\dist (5'b00001), .out(shifter_1_out));
  Shifter #(.width(32)) shifter_2 (.in(shifter_1_out), .\dist (5'b00001), .out(shifter_2_out));
  Adder #(.width(32)) adder_1 (.a(shifter_1_out), .b(n5_to_32_1_out_2), .out(adder_1_out));  // open: cin, cout
  Shifter #(.width(32)) shifter_3 (.in(shifter_2_out), .\dist (5'b00001), .out(shifter_3_out));
  Adder #(.width(32)) adder_2 (.a(shifter_2_out), .b(adder_1_out), .out(adder_2_out));  // open: cin, cout
  Adder #(.width(32)) adder_3 (.a(shifter_3_out), .b(adder_2_out), .out(out_2));  // open: cin, cout
endmodule

// left_bat
module bat_move (
  input  [7:0] in_1,
  input  in_2,
  input  in_3,
  output [7:0] bat_y
);

  wire adder_1_cout, adder_2_cout, adder_3_cout, adder_4_cout, comparator_1_gt, controlled_buffer_1_out,
       controlled_buffer_2_out, not_1_out, or_1_out;
  wire [7:0] adder_3_out, adder_4_out, multiplexer_1_out, multiplexer_2_out, undriven, y;

  Adder adder_1 (.a(in_1), .b(8'h21), .cout(adder_1_cout));  // open: out, cin
  or or_1 (or_1_out, adder_1_cout, adder_3_cout);
  not not_1 (not_1_out, or_1_out);
  assign controlled_buffer_1_out = not_1_out ? in_2 : 1'bz;  // Controlled_Buffer controlled_buffer_1
  assign controlled_buffer_2_out = adder_4_cout ? in_3 : 1'bz;  // Controlled_Buffer controlled_buffer_2
  Adder adder_2 (.a(undriven), .b(y), .cout(adder_2_cout));  // open: out, cin
  // AND_Gate and_1 has open pins: in0=adder_2_cout, in1=comparator_1_gt, out=open
  Multiplexer #(.width(8)) multiplexer_1 (
    .in0(in_1), .in1(adder_3_out), .out(multiplexer_1_out), .sel(controlled_buffer_1_out));  // open: en
  Adder adder_3 (.a(in_1), .b(8'h7), .out(adder_3_out), .cout(adder_3_cout));  // open: cin
  Pull_Resistor pull_resistor_1 (.node(controlled_buffer_1_out));
  Multiplexer #(.width(8)) multiplexer_2 (
    .in0(in_1), .in1(adder_4_out), .out(multiplexer_2_out), .sel(controlled_buffer_2_out));  // open: en
  Adder adder_4 (.a(in_1), .b(8'hf9), .out(adder_4_out), .cout(adder_4_cout));  // open: cin
  Pull_Resistor pull_resistor_2 (.node(controlled_buffer_2_out));
  Comparator comparator_1 (.a(undriven), .b({8{1'b0}}), .gt(comparator_1_gt));  // open: eq, lt
  Multiplexer #(.width(8)) multiplexer_3 (
    .in0(multiplexer_1_out), .in1(multiplexer_2_out), .out(bat_y), .sel(controlled_buffer_2_out));  // open: en
endmodule

module leds (
  input  [7:0] in_1,
  input  [7:0] in_2,
  output out_3,
  output out_4,
  output out_5,
  output out_6,
  output out_7,
  output out_8,
  output out_9,
  output out_10,
  output out_11,
  output out_12,
  output out_13,
  output out_14,
  output out_15,
  output out_16,
  output out_17,
  output out_18,
  output out_19,
  output out_20,
  output out_21,
  output out_22,
  output out_23,
  output out_24,
  output out_25,
  output out_26,
  output out_27,
  output out_28,
  output out_29,
  output out_30,
  output out_31,
  output out_32,
  output out_33,
  output out_34
);

  wire clock_1_out, clock_2_out, comparator_1_eq, comparator_1_gt, comparator_2_eq, comparator_2_gt,
       controlled_buffer_1_out, controlled_buffer_2_out, or_1_out, or_2_out, or_3_out;
  wire [31:0] multiplexer_2_out, multiplexer_3_out;

  Clock #(.highDuration(100), .lowDuration(100)) clock_1 (.out(clock_1_out));
  Comparator comparator_1 (.a(in_1), .b(8'h18), .gt(comparator_1_gt), .eq(comparator_1_eq));  // open: lt
  Comparator comparator_2 (.a(in_2), .b(8'h18), .gt(comparator_2_gt), .eq(comparator_2_eq));  // open: lt
  assign controlled_buffer_1_out = or_3_out ? clock_1_out : 1'bz;  // Controlled_Buffer controlled_buffer_1
  or or_1 (or_1_out, comparator_1_gt, comparator_1_eq);
  or or_2 (or_2_out, comparator_2_gt, comparator_2_eq);
  or or_3 (or_3_out, or_1_out, or_2_out);
  Multiplexer #(.width(32)) multiplexer_1 (
    .in0(multiplexer_2_out), .in1(multiplexer_3_out),
    .out({out_33, out_31, out_29, out_27, out_25, out_23, out_21, out_19, out_17, out_15, out_13, out_11, out_9, out_7, out_5, out_3, out_4, out_6, out_8, out_10, out_12, out_14, out_16, out_18, out_20, out_22, out_24, out_26, out_28, out_30, out_32, out_34}),
    .sel(or_3_out));  // open: en
  Multiplexer #(.width(32)) multiplexer_2 (
    .in0(32'h55555555), .in1(32'haaaaaaaa), .out(multiplexer_2_out), .sel(controlled_buffer_1_out));  // open: en
  Multiplexer #(.width(32)) multiplexer_3 (
    .in0({32{1'b1}}), .in1({32{1'b0}}), .out(multiplexer_3_out), .sel(controlled_buffer_2_out));  // open: en
  assign controlled_buffer_2_out = or_3_out ? clock_2_out : 1'bz;  // Controlled_Buffer controlled_buffer_2
  Clock #(.highDuration(100), .lowDuration(300)) clock_2 (.out(clock_2_out));
endmodule

module ball_move (
  input  crash_x,
  input  crash_y,
  input  [7:0] vx,
  input  [7:0] vy,
  input  [7:0] ball_x,
  input  [7:0] ball_y,
  output [7:0] ball_x_2,
  output [7:0] ball_y_2,
  output [7:0] new_vx,
  output [7:0] new_vy
);

  wire [7:0] if_1_res, if_2_res, inc_8_bit_2_out_2, neg_vx, not_1_out, not_2_out;

  assign not_1_out = ~vx;  // NOT_Gate not_1, 8 bits wide
  assign not_2_out = ~vy;  // NOT_Gate not_2, 8 bits wide
  \if  if_1 (.A(vx), .sel(crash_x), .B(neg_vx), .res(if_1_res));
  inc_8_bit inc_8_bit_1 (.in_1(not_1_out), .out_2(neg_vx));
  \if  if_2 (.A(vy), .sel(crash_y), .B(inc_8_bit_2_out_2), .res(if_2_res));
  inc_8_bit inc_8_bit_2 (.in_1(not_2_out), .out_2(inc_8_bit_2_out_2));
  Adder adder_1 (.a(if_1_res), .b(ball_x), .out(ball_x_2));  // open: cin, cout
  Adder adder_2 (.a(if_2_res), .b(ball_y), .out(ball_y_2));  // open: cin, cout
  Multiplexer #(.width(8)) multiplexer_1 (.in0(vx), .in1(neg_vx), .out(new_vx), .sel(crash_x));  // open: en
  Multiplexer #(.width(8)) multiplexer_2 (.in0(vy), .in1(inc_8_bit_2_out_2), .out(new_vy), .sel(crash_y));  // open: en
endmodule

module \if  (
  input  [7:0] A,
  input  sel,
  input  [7:0] B,
  output [7:0] res
);

  wire [7:0] and_1_out, and_2_out;
  wire [7:7] not_1_out;

  not not_1 (not_1_out[7], sel);
  assign and_1_out = A & {8{not_1_out[7]}};  // AND_Gate and_1, 8 bits wide
  assign and_2_out = {8{sel}} & B;  // AND_Gate and_2, 8 bits wide
  assign res = and_1_out | and_2_out;  // OR_Gate or_1, 8 bits wide
endmodule

module check_hit (
  input  [7:0] left_bat,
  input  [7:0] right_bat,
  input  [7:0] vx,
  input  [7:0] ball_x,
  input  [7:0] vy,
  input  [7:0] ball_y,
  output x_hit,
  output hitTheRightWall,
  output hitTheLeftWall,
  output y_hit
);

  wire adder_1_cout, adder_2_cout, adder_3_cout, adder_4_cout, and_2_out, and_3_out, and_4_out, and_5_out,
       and_6_out, check_carry_2_out_3, comparator_1_lt, comparator_2_lt, comparator_3_gt, comparator_4_gt,
       comparator_5_lt, comparator_6_eq, comparator_6_gt, comparator_7_eq, comparator_8_lt, comparator_9_eq,
       comparator_9_gt, comparator_10_eq, or_1_out, or_3_out, or_4_out;
  wire [15:0] adder_5_out, adder_6_out, bit_extender_1_out, bit_extender_2_out, bit_extender_3_out,
       bit_extender_4_out;

  Adder adder_1 (.a(ball_x), .b(vx), .cout(adder_1_cout));  // open: out, cin
  Comparator comparator_1 (.a(vx), .b({8{1'b0}}), .lt(comparator_1_lt));  // open: gt, eq
  Adder adder_2 (.a(ball_y), .b(vy), .cout(adder_2_cout));  // open: out, cin
  Comparator comparator_2 (.a(vy), .b({8{1'b0}}), .lt(comparator_2_lt));  // open: gt, eq
  assign bit_extender_1_out = {{8{1'b0}}, {left_bat[7:3], 3'b000}};  // Bit_Extender bit_extender_1
  assign bit_extender_2_out = {{8{1'b0}}, {right_bat[7:3], 3'b000}};  // Bit_Extender bit_extender_2
  Adder adder_3 (.a(vx), .b(ball_x), .cout(adder_3_cout));  // open: out, cin
  and and_1 (hitTheRightWall, adder_3_cout, comparator_3_gt);
  check_carry check_carry_1 (.in_1(comparator_1_lt), .in_2(adder_1_cout), .out_3(hitTheLeftWall));
  Adder adder_4 (.a(vy), .b(ball_y), .cout(adder_4_cout));  // open: out, cin
  and and_2 (and_2_out, adder_4_cout, comparator_4_gt);
  check_carry check_carry_2 (.in_1(comparator_2_lt), .in_2(adder_2_cout), .out_3(check_carry_2_out_3));
  Adder #(.width(16)) adder_5 (.a(16'h21), .b(bit_extender_1_out), .out(adder_5_out));  // open: cin, cout
  assign bit_extender_3_out = {{8{1'b0}}, ball_y};  // Bit_Extender bit_extender_3
  Adder #(.width(16)) adder_6 (.a(16'h21), .b(bit_extender_2_out), .out(adder_6_out));  // open: cin, cout
  Comparator comparator_3 (.a(vx), .b({8{1'b0}}), .gt(comparator_3_gt));  // open: eq, lt
  or or_1 (or_1_out, hitTheRightWall, hitTheLeftWall);
  Comparator comparator_4 (.a(vy), .b({8{1'b0}}), .gt(comparator_4_gt));  // open: eq, lt
  or or_2 (y_hit, and_2_out, check_carry_2_out_3);
  Comparator #(.width(16), .mode("unsigned")) comparator_5 (
    .a(bit_extender_3_out), .b(adder_5_out), .lt(comparator_5_lt));  // open: gt, eq
  Comparator #(.mode("unsigned")) comparator_6 (
    .a(ball_y), .b({left_bat[7:3], 3'b000}), .gt(comparator_6_gt), .eq(comparator_6_eq));  // open: lt
  Comparator #(.width(5), .mode("unsigned")) comparator_7 (
    .a(5'b00001), .b(ball_x[7:3]), .eq(comparator_7_eq));  // open: gt, lt
  assign bit_extender_4_out = {{8{1'b0}}, ball_y};  // Bit_Extender bit_extender_4
  or or_3 (or_3_out, comparator_6_gt, comparator_6_eq);
  Comparator #(.width(16), .mode("unsigned")) comparator_8 (
    .a(bit_extender_4_out), .b(adder_6_out), .lt(comparator_8_lt));  // open: gt, eq
  Comparator #(.mode("unsigned")) comparator_9 (
    .a(ball_y), .b({right_bat[7:3], 3'b000}), .gt(comparator_9_gt), .eq(comparator_9_eq));  // open: lt
  or or_4 (or_4_out, comparator_9_gt, comparator_9_eq);
  Comparator #(.width(5), .mode("unsigned")) comparator_10 (
    .a(5'b11110), .b(ball_x[7:3]), .eq(comparator_10_eq));  // open: gt, lt
  and and_3 (and_3_out, comparator_5_lt, or_3_out);
  and and_4 (and_4_out, comparator_8_lt, or_4_out);
  and and_5 (and_5_out, and_3_out, comparator_7_eq);
  and and_6 (and_6_out, and_4_out, comparator_10_eq);
  or or_5 (x_hit, and_5_out, and_6_out, or_1_out);

  // Other names for the same wires on the sheet: x[7:0] = ball_x; y[7:0] = ball_y
endmodule

module inc_8_bit (
  input  [7:0] in_1,
  output [7:0] out_2
);

  wire [7:1] and_1_out;
  wire [7:7] and_1_out_2;

  assign {and_1_out_2[7], and_1_out} = {and_1_out, 1'b1} & in_1;  // AND_Gate and_1, 8 bits wide
  assign out_2 = in_1 ^ {and_1_out, 1'b1};  // XOR_Gate xor_1, 8 bits wide
  // also tied to GND on the sheet: and_1_out_2[7]
endmodule

module check_carry (
  input  in_1,
  input  in_2,
  output out_3
);

  wire transistor_1_out;

  Transistor #(.\type ("n")) transistor_1 (.in(1'b1), .out(transistor_1_out), .gate(in_1));
  Pull_Resistor pull_resistor_1 (.node(out_3));
  Transistor #(.gate("br")) transistor_2 (.in(transistor_1_out), .out(out_3), .gate(in_2));
endmodule

// right_bat
module cdm8_bat_move (
  input  [7:0] current_y,
  input  [7:0] new_y,
  output [7:0] out_3
);

  wire adder_1_cout, adder_2_cout, adder_3_cout, comparator_1_gt, comparator_1_lt, controlled_buffer_1_out,
       controlled_buffer_2_out, not_1_out, or_1_out;
  wire [7:0] adder_2_out, adder_3_out, multiplexer_1_out, multiplexer_2_out;

  Comparator #(.mode("unsigned")) comparator_1 (
    .a(current_y), .b(new_y), .gt(comparator_1_gt), .lt(comparator_1_lt));  // open: eq
  Adder adder_1 (.a(current_y), .b(8'h21), .cout(adder_1_cout));  // open: out, cin
  or or_1 (or_1_out, adder_1_cout, adder_2_cout);
  not not_1 (not_1_out, or_1_out);
  assign controlled_buffer_1_out = not_1_out ? comparator_1_lt : 1'bz;  // Controlled_Buffer controlled_buffer_1
  Adder adder_2 (.a(current_y), .b(8'h1), .out(adder_2_out), .cout(adder_2_cout));  // open: cin
  Adder adder_3 (.a(current_y), .b({8{1'b1}}), .out(adder_3_out), .cout(adder_3_cout));  // open: cin
  assign controlled_buffer_2_out = adder_3_cout ? comparator_1_gt : 1'bz;  // Controlled_Buffer controlled_buffer_2
  Multiplexer #(.width(8)) multiplexer_1 (
    .in0(current_y), .in1(adder_2_out), .out(multiplexer_1_out), .sel(controlled_buffer_1_out));  // open: en
  Pull_Resistor pull_resistor_1 (.node(controlled_buffer_1_out));
  Multiplexer #(.width(8)) multiplexer_2 (
    .in0(current_y), .in1(adder_3_out), .out(multiplexer_2_out), .sel(controlled_buffer_2_out));  // open: en
  Pull_Resistor pull_resistor_2 (.node(controlled_buffer_2_out));
  Multiplexer #(.width(8)) multiplexer_3 (
    .in0(multiplexer_1_out), .in1(multiplexer_2_out), .out(out_3), .sel(controlled_buffer_2_out));  // open: en
endmodule

// cdm8 with banks
module cdm8 (
  input  reset,
  input  [7:0] p_score,
  input  [7:0] cdm8_score,
  input  [7:0] ball_x,
  input  [7:0] ball_y,
  input  [7:0] vx,
  input  [7:0] vy,
  output [7:0] out_8,
  output [7:0] out_9
);

  wire and_2_out, and_3_out, cdm_8_mark5_1_p4, cdm_8_mark5_1_p5, cdm_8_mark5_1_p7, cdm_8_mark5_1_p8,
       cdm_8_mark5_1_p10, cdm_8_mark5_1_p11, clk, clk1, comparator_1_eq, comparator_2_eq, comparator_3_eq,
       controlled_buffer_3_out, d_ff_1_q, decoder_1_out0, decoder_1_out1, IAck, IOsel, IRQ,
       multiplexer_1_out, multiplexer_4_out, not_1_out, not_2_out, not_3_out, not_4_out, of, or_1_out, ram,
       READwrite, register_3_q;
  wire [2:0] cnt, vec;
  wire [7:0] addr, address, bit_extender_1_out, cdm_8_mark5_1_p14, cdm_8_mark5_1_p15, IOdat,
       multiplexer_2_out, multiplexer_3_out, pc;

  // Probe on ball_y
  // Probe on cdm_8_mark5_1_p8
  // Probe on cdm_8_mark5_1_p5
  // Probe on cdm_8_mark5_1_p7
  // Probe on cdm_8_mark5_1_p4
  Multiplexer multiplexer_1 (.in0(1'b0), .in1(clk), .out(multiplexer_1_out), .sel(ram), .en(of));
  // Probe on ball_x
  // Probe on vx
  // Probe on pc
  // CdM_8_mark5 cdm_8_mark5_1: pin names not known; wires that end beside it: IRQ, vec, IAck, cdm_8_mark5_1_p4, cdm_8_mark5_1_p5, multiplexer_1_out, cdm_8_mark5_1_p7, cdm_8_mark5_1_p8, pc, cdm_8_mark5_1_p10, cdm_8_mark5_1_p11, READwrite, address, cdm_8_mark5_1_p14, cdm_8_mark5_1_p15
  Multiplexer #(.select(3), .width(8)) multiplexer_2 (
    .in0(p_score), .in1(cdm8_score), .in2(out_8), .in3(ball_x), .in4(ball_y), .in5(vx), .in6(vy),
    .in7(IOdat), .out(multiplexer_2_out), .sel(cnt));  // open: en
  // Probe on vy
  and and_1 (IOsel, address[4], address[5], address[6], address[7], decoder_1_out1);
  // Probe on multiplexer_2_out
  // Probe on addr
  // Probe on address
  Decoder #(.disabled(0)) decoder_1 (
    .out0(decoder_1_out0), .out1(decoder_1_out1), .sel(cdm_8_mark5_1_p10), .en(cdm_8_mark5_1_p11));
  not not_1 (not_1_out, READwrite);
  assign IOdat = not_1_out ? cdm_8_mark5_1_p14 : 8'bz;  // Controlled_Buffer controlled_buffer_1
  assign cdm_8_mark5_1_p15 = READwrite ? IOdat : 8'bz;  // Controlled_Buffer controlled_buffer_2
  Multiplexer #(.width(8)) multiplexer_3 (
    .in0(addr), .in1(address), .out(multiplexer_3_out), .sel(and_2_out));  // open: en
  and and_2 (and_2_out, ram, of);
  // Probe on address
  and and_3 (and_3_out, decoder_1_out1, ~IOsel);  // AND_Gate
  Comparator comparator_1 (.a(8'he2), .b(address), .eq(comparator_1_eq));  // open: gt, lt
  // Probe on multiplexer_3_out
  or or_1 (or_1_out, and_3_out, ~of);  // OR_Gate
  not not_2 (not_2_out, clk);
  Register register_1 (.D(IOdat), .Q(out_8), .clk(comparator_1_eq));  // open: en, clr
  RAM #(.bus("separate")) ram_1 (
    .addr(multiplexer_3_out), .din(multiplexer_2_out), .data(IOdat), .sel(or_1_out), .clk(not_2_out),
    .ld(multiplexer_4_out), .clr(reset));  // open: str
  Multiplexer multiplexer_4 (.in0(1'b0), .in1(READwrite), .out(multiplexer_4_out), .sel(of));  // open: en
  ROM rom_1 (.addr(address), .data(IOdat), .sel(decoder_1_out0));
  Comparator comparator_2 (.a(8'he7), .b(address), .eq(comparator_2_eq));  // open: gt, lt
  // Probe on IOdat
  Register register_2 (.D(IOdat), .Q(out_9), .clk(comparator_2_eq));  // open: en, clr
  Clock clock_1 (.out(clk));
  Multiplexer multiplexer_5 (.in0(clk), .in1(1'b0), .out(clk1), .sel(d_ff_1_q));  // open: en
  D_Flip_Flop d_ff_1 (.clk(of), .D(of), .Q(d_ff_1_q), .reset(comparator_3_eq));  // open: Qn, preset, en
  D_Flip_Flop #(.trigger("high")) d_ff_2 (.clk(d_ff_1_q), .D(d_ff_1_q), .Q(ram));  // open: Qn, preset, en, reset
  assign bit_extender_1_out = {{5{1'b0}}, cnt};  // Bit_Extender bit_extender_1
  Counter #(.width(3), .max('h7)) counter_1 (
    .Q(cnt), .carry(of), .clk(clk1), .clr(controlled_buffer_3_out));  // open: load, D, count
  assign controlled_buffer_3_out = of ? register_3_q : 1'bz;  // Controlled_Buffer controlled_buffer_3
  not not_3 (not_3_out, register_3_q);
  Comparator comparator_3 (.a(pc), .b(8'h2b), .eq(comparator_3_eq));  // open: gt, lt
  Adder adder_1 (.a(8'he0), .b(bit_extender_1_out), .out(addr));  // open: cin, cout
  Register #(.width(1)) register_3 (
    .D(not_3_out), .Q(register_3_q), .clk(comparator_3_eq), .clr(not_4_out));  // open: en
  not not_4 (not_4_out, of);

  // Other names for the same wires on the sheet: IOaddr[3:0] = address[3:0]; bat[7:0] = out_8;
  //   player_score[7:0] = p_score

  // Notes on the sheet:
  //   contents of rom_1 (hex, n*v repeats v):
  //   cd f0 d1 e3 b5 d3 e5 bf f e4 e 5 e5 10 ee 2b d0 f0 31 5 99 d3 e6 bf f e5 1c 85 d2 e4 ba 19 e3 25 d2
  //   ff 36 d3 ff 3e d0 e2 a2 ee 2 d7 d4
endmodule
